# Fritzing sketch stm-den (saved by Fritzing 1.0.1rc)

parts:
  Деталь1 = STM32F407G-DISC1
  IC1 = 2.8 inch LCD SPI display with touch screen & SD card [mn=Screen]
  Деталь2 = Real Time Clock Module - DS1307 RTC Breakout Board [mn=HW-111]
  Деталь3 = BME280 Breakout
  JP1 = Header 3 [mn=UART package=screwterminal-3.5mm-3_lock.007s]

nets:
  N1: Деталь1.pin7, IC1.pin5
  N2: Деталь1.pin8, IC1.pin7
  N3: Деталь1.pin9, IC1.pin6
  GND: Деталь1.pin12, Деталь1.pin76, Деталь1.pin100, IC1.pin2, Деталь2.GND, Деталь3.GND, JP1.1
  N4: Деталь1.pin18, Деталь3.SDI/SDA
  N5: Деталь1.pin31, IC1.pin8
  N6: Деталь1.pin32, IC1.pin4
  N7: Деталь1.pin33, IC1.pin3
  N8: Деталь1.pin34, IC1.pin_9
  N9: Деталь1.pin42, Деталь3.SCK/SCL
  5V: Деталь1.pin52, Деталь1.pin77, IC1.pin1, Деталь2.5V, Деталь3.3.3V
  N10: Деталь1.pin62, Деталь2.SCL
  N11: Деталь1.pin69, JP1.2
  N12: Деталь1.pin87, Деталь2.SDA
  N13: Деталь1.pin94, JP1.3

notes:
  MISO
  LED
  SCK
  MOSI
  DC
  RST
  CS
  UART4
  GND
  Rx
  Tx
  2.8" TFT LCD SPI 240x320 v1.1
  MSP2807 Module
  Driver ILI9341
  5v
  SCL
  SDA
  I2C-1
  I2C-2
  SPI1

custom parts:
  STM32F407G-DISC1: The STM32F4DISCOVERY Discovery kit allows users to easily develop applications with the STM32F407VG high-performance microcontroller with the Arm® Cortex®-M4 32-bit core. It includes everything required either for beginners or experienced users to get started quickly. Based on STM32F407VG, it includes an ST-LINK/V2-A embedded debug tool, one STMEMS digital accelerometer, one digital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
  2.8 inch LCD SPI display with touch screen & SD card: A generic 2.8 inch LCD TFT 320x280 display with touchscreen and SD card slot.
